# Fritzing sketch 8bit-gmail-notifier (saved by Fritzing 0.9.3b)
breadboards: 2

parts:
  Part1 = FTDI Basic Programmer
  U1 = LCD-16X2 [package=lcd-16x2]
  IC1 = ATmega16 [package="DIP (Dual Inline)"]
  X1 = USB Connectors [package=usb-mb-h]
  AtTiny2313-20PU1 = IC, DIP package, 20 pins [chip_label=AtTiny2313-20PU spacing=300mil]
  R4 = Trimmer Potentiometer [maximum_resistance=10kΩ package=THT]
  LED1 = LED - 3mm [color="Red (633nm)" package="3 mm [THT]"]
  LED2 = LED - 3mm [color="Green (555nm)" package="3 mm [THT]"]
  74HC3 = 74HC164 [package="DIP (Dual Inline) [THT]"]
  SG3 = Buzzer 12mm [package=buzzer-12mm-ns]
  DI1 = 7-Segment LED Display [package=THT]
  D1 = Zener Diode [part_number=1N4732A breakdown_voltage=3.6V package="Melf DO-213 AB [SMD]"]
  D2 = Zener Diode [part_number=1N4732A breakdown_voltage=3.6V package="Melf DO-213 AB [SMD]"]
  22pF = Capacitor [package=cap-pth-small2]
  22pF_2 = Capacitor [package=cap-pth-small2]
  R7 = Resistor [tolerance=±5% resistance=330 package=THT]
  R6 = Resistor [tolerance=±5% resistance=1.5k package=THT]
  R5 = Resistor [tolerance=±5% resistance=1.5k package=THT]
  R8 = Resistor [tolerance=±5% resistance=1.5k package=THT]
  R9 = Resistor [tolerance=±5% resistance=68 package=THT]
  R10 = Resistor [tolerance=±5% resistance=68 package=THT]
  C1 = Electrolytic Capacitor [capacitance=47µF voltage=10V package="1010 [SMD, electrolytic]"]
  XTAL4 = Crystal [package=THT]
  R11 = Resistor [tolerance=±5% resistance=10k package=THT]

nets:
  N1: Part1.RXI, IC1.PIN_15
  N2: Part1.TXO, IC1.PIN_14
  VDD: Part1.POWER, U1.VDD, U1.A, IC1.PIN_10, X1.VBUS, AtTiny2313-20PU1.pin20, R4.leg2, 74HC3.CLR, 74HC3.VCC, R7.Pin_0, R6.Pin_1, C1.+, R11.Pin_1
  GND: Part1.GND, U1.VSS, U1.R_W, U1.K, IC1.PIN_11, X1.GND, AtTiny2313-20PU1.pin10, R4.leg1, LED1.cathode, LED2.cathode, 74HC3.GND, SG3.2, D1.anode, D2.anode, 22pF.1, 22pF_2.2, C1.-
  N3: U1.VO, R4.wiper
  N4: U1.RS, IC1.PIN_34
  N5: U1.E, IC1.PIN_33
  N6: U1.DB4, IC1.PIN_24
  N7: U1.DB5, IC1.PIN_25
  N8: U1.DB6, IC1.PIN_26
  N9: U1.DB7, IC1.PIN_27
  N10: IC1.PIN_6, AtTiny2313-20PU1.pin17
  N11: IC1.PIN_7, AtTiny2313-20PU1.pin18
  N12: IC1.PIN_8, AtTiny2313-20PU1.pin19
  N13: IC1.PIN_9, AtTiny2313-20PU1.pin16
  N14: IC1.PIN_16, 74HC3.CLK
  N15: IC1.PIN_17, 74HC3.A, 74HC3.B
  N16: IC1.PIN_18, SG3.1
  N17: X1.D+, D1.cathode, R10.Pin_0
  N18: X1.D-, D2.cathode, R6.Pin_0, R9.Pin_0
  N19: AtTiny2313-20PU1.pin1, R11.Pin_0
  N20: AtTiny2313-20PU1.pin4, 22pF_2.1, XTAL4.pin_1
  N21: AtTiny2313-20PU1.pin5, 22pF.2, XTAL4.pin_0
  N22: AtTiny2313-20PU1.pin6, R10.Pin_1
  N23: AtTiny2313-20PU1.pin7, R9.Pin_1
  N24: AtTiny2313-20PU1.pin9, R5.Pin_1
  N25: AtTiny2313-20PU1.pin12, R8.Pin_1
  N26: LED1.anode, R5.Pin_0
  N27: LED2.anode, R8.Pin_0
  N28: 74HC3.QA, DI1.cathodeE
  N29: 74HC3.QB, DI1.cathodeD
  N30: 74HC3.QC, DI1.cathodeC
  N31: 74HC3.QD, DI1.cathodeDP
  N32: 74HC3.QE, DI1.cathodeG
  N33: 74HC3.QF, DI1.cathodeF
  N34: 74HC3.QG, DI1.cathodeA
  N35: 74HC3.QH, DI1.cathodeB
  N36: DI1.commAnode#7, R7.Pin_1

custom parts:
  ATmega16: ATmega16 - 40 pins, 600 mil dual inline package (DIP)
  74HC164: 8-Bit Parallel-Out Serial Shift Registers
